# Fritzing sketch gc_controller (saved by Fritzing 0.9.4)
perfboards: 1

parts:
  J1 = female pin header, 20 pins [form="♀ (female)"]
  J2 = female pin header, 20 pins [form="♀ (female)"]
  U1 = atmega328 [package=dip]
  Y1 = CRYSTAL [package=crystal-smd-5x3]
  Part1 = Logic Level Converter
  C1 = Capacitor [package=cap-pth-small]
  C2 = Capacitor [package=cap-pth-small]  # not connected
  J3 = female pin header, 5 pins [form="♀ (female)"]

nets:
  N1: J1.pin16, Part1.RX2_LV
  N2: J1.pin17, Part1.TX2_LV
  N3: J2.pin20, Part1.LV
  N4: U1.D0_(RX), Part1.RX2_HV
  N5: U1.D1_(TX), Part1.TX2_HV
  N6: U1.XLAT1, Y1.2, C1.2
  N7: U1.XLAT2, Y1.1
  N8: U1.D8, Part1.TX_HV
  N9: Part1.TX_LV, J3.pin1
